// Logisim project Automat_Iluminare_Variabila.circ as structural Verilog
module main (
  input  in_inc,
  input  in_dec,
  input  in_rst,
  input  in_ok,
  input  in_clk,
  output [6:0] cathode,
  output [7:0] anode,
  output [7:0] L01234568
);

  wire and_gate_1_x, clk_256_pe_per_hz_1_clk_gen, dec, div_freq_2hz_1_clk_2hz, en_tst, inc, ok, or_gate_1_x,
       rs_1_q, rst, uc_1_enable_auto, uc_1_enable_man;
  wire [1:0] m;
  wire [2:0] up_counter_1_counter;
  wire [3:0] binary_bcd_1_bcd0, binary_bcd_1_bcd1, binary_bcd_2_bcd0, binary_bcd_2_bcd1, binary_bcd_2_bcd2,
       mux_8_la_1_4bit_1_d_out, nr_auto_1_nr;
  wire [7:0] man_ctr_1_duty_cycle, mux_4_la_1_4bit_1_d_out, mux_4_la_1_8bit_1_d_out,
       mux_24_la_8_8bit_1_d_out0, mux_24_la_8_8bit_1_d_out1, mux_24_la_8_8bit_1_d_out2,
       mux_24_la_8_8bit_1_d_out3, mux_24_la_8_8bit_1_d_out4, mux_24_la_8_8bit_1_d_out5,
       mux_24_la_8_8bit_1_d_out6, mux_24_la_8_8bit_1_d_out7, numarator_1s_1_duty_cycle,
       numarator_2s_1_duty_cycle, numarator_3s_1_duty_cycle, numarator_4s_1_duty_cycle,
       numarator_5s_1_duty_cycle, numarator_6s_1_duty_cycle, numarator_7s_1_duty_cycle,
       numarator_8s_1_duty_cycle, triangular_1_wave_out;

  debouncer_30ns debouncer_30ns_1 (.btn(in_inc), .clk(in_clk), .btn_db(inc));
  debouncer_30ns debouncer_30ns_2 (.btn(in_dec), .clk(in_clk), .btn_db(dec));
  debouncer_30ns debouncer_30ns_3 (.btn(in_rst), .clk(in_clk), .btn_db(rst));
  debouncer_30ns debouncer_30ns_4 (.btn(in_ok), .clk(in_clk), .btn_db(ok));
  UC uc_1 (
    .inc(inc), .dec(dec), .rst(rst), .ok(ok), .clk(in_clk), .mode(m), .enable_man(uc_1_enable_man),
    .enable_auto(uc_1_enable_auto), .enable_test(en_tst));
  div_freq_2hz div_freq_2hz_1 (.clk_100mhz(in_clk), .clk_2hz(div_freq_2hz_1_clk_2hz));
  and_gate and_gate_1 (.a(rs_1_q), .b(uc_1_enable_auto), .x(and_gate_1_x));
  man_ctr man_ctr_1 (
    .inc(inc), .dec(dec), .clk(div_freq_2hz_1_clk_2hz), .rst(rst), .en(uc_1_enable_man),
    .duty_cycle(man_ctr_1_duty_cycle));
  nr_auto nr_auto_1 (
    .inc(inc), .dec(dec), .rst(rst), .clk(div_freq_2hz_1_clk_2hz), .en(and_gate_1_x), .nr(nr_auto_1_nr));
  RS rs_1 (.R(ok), .S(rst), .clk(in_clk), .Q(rs_1_q));
  numarator_1s numarator_1s_1 (.clk(in_clk), .en(en_tst), .rst(rst), .duty_cycle(numarator_1s_1_duty_cycle));
  numarator_2s numarator_2s_1 (.clk(in_clk), .en(en_tst), .rst(rst), .duty_cycle(numarator_2s_1_duty_cycle));
  numarator_3s numarator_3s_1 (.clk(in_clk), .en(en_tst), .rst(rst), .duty_cycle(numarator_3s_1_duty_cycle));
  numarator_4s numarator_4s_1 (.clk(in_clk), .en(en_tst), .rst(rst), .duty_cycle(numarator_4s_1_duty_cycle));
  numarator_5s numarator_5s_1 (.clk(in_clk), .en(en_tst), .rst(rst), .duty_cycle(numarator_5s_1_duty_cycle));
  numarator_6s numarator_6s_1 (.clk(in_clk), .en(en_tst), .rst(rst), .duty_cycle(numarator_6s_1_duty_cycle));
  numarator_7s numarator_7s_1 (.clk(in_clk), .en(en_tst), .rst(rst), .duty_cycle(numarator_7s_1_duty_cycle));
  numarator_8s numarator_8s_1 (.clk(in_clk), .en(en_tst), .rst(rst), .duty_cycle(numarator_8s_1_duty_cycle));
  or_gate or_gate_1 (.b(rs_1_q), .x(or_gate_1_x));  // open: a
  clk_256_pe_per_hz clk_256_pe_per_hz_1 (
    .n(nr_auto_1_nr), .rst(or_gate_1_x), .clk_100mhz(in_clk), .clk_gen(clk_256_pe_per_hz_1_clk_gen));
  triangular triangular_1 (.clk(clk_256_pe_per_hz_1_clk_gen), .reset(rst), .wave_out(triangular_1_wave_out));
  mux_4_la_1_4bit mux_4_la_1_4bit_1 (
    .din_0(4'b0000), .din_1(nr_auto_1_nr), .din_2(4'b0000), .din_3(4'b0000), .sel(m),
    .d_out(mux_4_la_1_4bit_1_d_out));
  mux_4_la_1_8bit mux_4_la_1_8bit_1 (
    .din_0(man_ctr_1_duty_cycle), .din_1(triangular_1_wave_out), .din_2({8{1'b0}}), .din_3({8{1'b0}}),
    .sel(m), .d_out(mux_4_la_1_8bit_1_d_out));
  mux_24_la_8_8bit mux_24_la_8_8bit_1 (
    .din_0(man_ctr_1_duty_cycle), .din_1(man_ctr_1_duty_cycle), .din_2(man_ctr_1_duty_cycle),
    .din_3(man_ctr_1_duty_cycle), .din_4(man_ctr_1_duty_cycle), .din_5(man_ctr_1_duty_cycle),
    .din_6(man_ctr_1_duty_cycle), .din_7(man_ctr_1_duty_cycle), .din_8(triangular_1_wave_out),
    .din_9(triangular_1_wave_out), .din_10(triangular_1_wave_out), .din_11(triangular_1_wave_out),
    .din_12(triangular_1_wave_out), .din_13(triangular_1_wave_out), .din_14(triangular_1_wave_out),
    .din_15(triangular_1_wave_out), .din_16(numarator_1s_1_duty_cycle), .din_17(numarator_2s_1_duty_cycle),
    .din_18(numarator_3s_1_duty_cycle), .din_19(numarator_4s_1_duty_cycle),
    .din_20(numarator_5s_1_duty_cycle), .din_21(numarator_6s_1_duty_cycle),
    .din_22(numarator_7s_1_duty_cycle), .din_23(numarator_8s_1_duty_cycle), .sel(m),
    .d_out0(mux_24_la_8_8bit_1_d_out0), .d_out1(mux_24_la_8_8bit_1_d_out1),
    .d_out2(mux_24_la_8_8bit_1_d_out2), .d_out3(mux_24_la_8_8bit_1_d_out3),
    .d_out4(mux_24_la_8_8bit_1_d_out4), .d_out5(mux_24_la_8_8bit_1_d_out5),
    .d_out6(mux_24_la_8_8bit_1_d_out6), .d_out7(mux_24_la_8_8bit_1_d_out7));
  binary_bcd binary_bcd_1 (
    .clk(in_clk), .reset(rst), .binary_in(mux_4_la_1_4bit_1_d_out), .bcd0(binary_bcd_1_bcd0),
    .bcd1(binary_bcd_1_bcd1));  // open: bcd2, bcd3, bcd4
  binary_bcd binary_bcd_2 (
    .clk(in_clk), .reset(rst), .binary_in(mux_4_la_1_8bit_1_d_out), .bcd0(binary_bcd_2_bcd0),
    .bcd1(binary_bcd_2_bcd1), .bcd2(binary_bcd_2_bcd2));  // open: bcd3, bcd4
  mux_8_la_1_4bit mux_8_la_1_4bit_1 (
    .din_0(binary_bcd_1_bcd0), .din_1(binary_bcd_1_bcd1), .din_2(4'b0000), .din_3(binary_bcd_2_bcd0),
    .din_4(binary_bcd_2_bcd1), .din_5(binary_bcd_2_bcd2), .din_6(4'b0000), .sel(up_counter_1_counter),
    .d_out(mux_8_la_1_4bit_1_d_out));  // open: din_7
  UP_COUNTER up_counter_1 (.clk(in_clk), .reset(rst), .counter(up_counter_1_counter));
  pwm pwm_1 (
    .clk(in_clk), .rst(rst), .duty_cycle0(mux_24_la_8_8bit_1_d_out0),
    .duty_cycle1(mux_24_la_8_8bit_1_d_out1), .duty_cycle2(mux_24_la_8_8bit_1_d_out2),
    .duty_cycle3(mux_24_la_8_8bit_1_d_out3), .duty_cycle4(mux_24_la_8_8bit_1_d_out4),
    .duty_cycle5(mux_24_la_8_8bit_1_d_out5), .duty_cycle6(mux_24_la_8_8bit_1_d_out6),
    .duty_cycle7(mux_24_la_8_8bit_1_d_out7), .led_out(L01234568));
  ssddecoder ssddecoder_1 (.enable(1'b1), .code(mux_8_la_1_4bit_1_d_out), .decode_ssd(cathode));
  mux_8_la_1_7bit mux_8_la_1_7bit_1 (
    .din_0(8'hfe), .din_1(8'hfd), .din_2({8{1'b1}}), .din_3(8'hf7), .din_4(8'hef), .din_5(8'hdf),
    .din_6({8{1'b1}}), .din_7(8'h7f), .sel(up_counter_1_counter), .d_out(anode));

  // Other names for the same wires on the sheet: clk = in_clk
endmodule

module mod_manual (
  input  inc,
  input  dec,
  input  en,
  input  rst,
  input  clk,
  output [7:0] Output_bus_1,
  output [7:0] Output_bus_2
);

  wire debouncer_30ns_1_btn_db, debouncer_30ns_2_btn_db, debouncer_30ns_3_btn_db, div_freq_2hz_1_clk_2hz;

  debouncer_30ns debouncer_30ns_1 (.btn(inc), .clk(clk), .btn_db(debouncer_30ns_1_btn_db));
  debouncer_30ns debouncer_30ns_2 (.btn(dec), .clk(clk), .btn_db(debouncer_30ns_2_btn_db));
  debouncer_30ns debouncer_30ns_3 (.btn(rst), .clk(clk), .btn_db(debouncer_30ns_3_btn_db));
  man_ctr man_ctr_1 (
    .inc(debouncer_30ns_1_btn_db), .dec(debouncer_30ns_2_btn_db), .clk(div_freq_2hz_1_clk_2hz),
    .rst(debouncer_30ns_3_btn_db), .en(en), .duty_cycle(Output_bus_1));
  div_freq_2hz div_freq_2hz_1 (.clk_100mhz(clk), .clk_2hz(div_freq_2hz_1_clk_2hz));
  pwm pwm_1 (
    .clk(clk), .rst(debouncer_30ns_3_btn_db), .duty_cycle0(Output_bus_1), .duty_cycle1(Output_bus_1),
    .duty_cycle2(Output_bus_1), .duty_cycle3(Output_bus_1), .duty_cycle4(Output_bus_1),
    .duty_cycle5(Output_bus_1), .duty_cycle6(Output_bus_1), .duty_cycle7(Output_bus_1), .led_out(Output_bus_2));
endmodule

module mod_automat (
  input  inc,
  input  dec,
  input  ok,
  input  rst,
  input  clk,
  output [3:0] Output_bus_2,
  output [7:0] Output_bus_1
);

  wire clk_256_pe_per_hz_1_clk_gen, debouncer_30ns_1_btn_db, debouncer_30ns_2_btn_db,
       debouncer_30ns_3_btn_db, debouncer_30ns_4_btn_db, div_freq_2hz_1_clk_2hz, or_gate_1_x, rs_1_q;
  wire [7:0] triangular_1_wave_out;

  debouncer_30ns debouncer_30ns_1 (.btn(inc), .clk(clk), .btn_db(debouncer_30ns_1_btn_db));
  debouncer_30ns debouncer_30ns_2 (.btn(dec), .clk(clk), .btn_db(debouncer_30ns_2_btn_db));
  debouncer_30ns debouncer_30ns_4 (.btn(ok), .clk(clk), .btn_db(debouncer_30ns_4_btn_db));
  debouncer_30ns debouncer_30ns_3 (.btn(rst), .clk(clk), .btn_db(debouncer_30ns_3_btn_db));
  div_freq_2hz div_freq_2hz_1 (.clk_100mhz(clk), .clk_2hz(div_freq_2hz_1_clk_2hz));
  nr_auto nr_auto_1 (
    .inc(debouncer_30ns_1_btn_db), .dec(debouncer_30ns_2_btn_db), .rst(debouncer_30ns_3_btn_db),
    .clk(div_freq_2hz_1_clk_2hz), .en(rs_1_q), .nr(Output_bus_2));
  RS rs_1 (.R(debouncer_30ns_4_btn_db), .S(debouncer_30ns_3_btn_db), .clk(clk), .Q(rs_1_q));
  or_gate or_gate_1 (.a(debouncer_30ns_3_btn_db), .b(rs_1_q), .x(or_gate_1_x));
  clk_256_pe_per_hz clk_256_pe_per_hz_1 (
    .n(Output_bus_2), .rst(or_gate_1_x), .clk_100mhz(clk), .clk_gen(clk_256_pe_per_hz_1_clk_gen));
  triangular triangular_1 (
    .clk(clk_256_pe_per_hz_1_clk_gen), .reset(debouncer_30ns_3_btn_db), .wave_out(triangular_1_wave_out));
  pwm pwm_1 (
    .clk(clk), .rst(debouncer_30ns_3_btn_db), .duty_cycle0(triangular_1_wave_out),
    .duty_cycle1(triangular_1_wave_out), .duty_cycle2(triangular_1_wave_out),
    .duty_cycle3(triangular_1_wave_out), .duty_cycle4(triangular_1_wave_out),
    .duty_cycle5(triangular_1_wave_out), .duty_cycle6(triangular_1_wave_out),
    .duty_cycle7(triangular_1_wave_out), .led_out(Output_bus_1));
endmodule

module mod_test (
  input  clk,
  input  rst,
  input  en,
  output [7:0] Output_bus_1
);

  wire debouncer_30ns_3_btn_db;
  wire [7:0] numarator_1s_1_duty_cycle, numarator_2s_1_duty_cycle, numarator_3s_1_duty_cycle,
       numarator_4s_1_duty_cycle, numarator_5s_1_duty_cycle, numarator_6s_1_duty_cycle,
       numarator_7s_1_duty_cycle, numarator_8s_1_duty_cycle;

  debouncer_30ns debouncer_30ns_3 (.btn(rst), .clk(clk), .btn_db(debouncer_30ns_3_btn_db));
  numarator_1s numarator_1s_1 (
    .clk(clk), .en(en), .rst(debouncer_30ns_3_btn_db), .duty_cycle(numarator_1s_1_duty_cycle));
  numarator_2s numarator_2s_1 (
    .clk(clk), .en(en), .rst(debouncer_30ns_3_btn_db), .duty_cycle(numarator_2s_1_duty_cycle));
  numarator_3s numarator_3s_1 (
    .clk(clk), .en(en), .rst(debouncer_30ns_3_btn_db), .duty_cycle(numarator_3s_1_duty_cycle));
  numarator_4s numarator_4s_1 (
    .clk(clk), .en(en), .rst(debouncer_30ns_3_btn_db), .duty_cycle(numarator_4s_1_duty_cycle));
  numarator_5s numarator_5s_1 (
    .clk(clk), .en(en), .rst(debouncer_30ns_3_btn_db), .duty_cycle(numarator_5s_1_duty_cycle));
  numarator_6s numarator_6s_1 (
    .clk(clk), .en(en), .rst(debouncer_30ns_3_btn_db), .duty_cycle(numarator_6s_1_duty_cycle));
  numarator_7s numarator_7s_1 (
    .clk(clk), .en(en), .rst(debouncer_30ns_3_btn_db), .duty_cycle(numarator_7s_1_duty_cycle));
  numarator_8s numarator_8s_1 (
    .clk(clk), .en(en), .rst(debouncer_30ns_3_btn_db), .duty_cycle(numarator_8s_1_duty_cycle));
  pwm pwm_1 (
    .clk(clk), .rst(debouncer_30ns_3_btn_db), .duty_cycle0(numarator_1s_1_duty_cycle),
    .duty_cycle1(numarator_2s_1_duty_cycle), .duty_cycle2(numarator_3s_1_duty_cycle),
    .duty_cycle3(numarator_4s_1_duty_cycle), .duty_cycle4(numarator_5s_1_duty_cycle),
    .duty_cycle5(numarator_6s_1_duty_cycle), .duty_cycle6(numarator_7s_1_duty_cycle),
    .duty_cycle7(numarator_8s_1_duty_cycle), .led_out(Output_bus_1));
endmodule

// VHDL entity ssddecoder, as the project stores it:
LIBRARY ieee;
USE ieee.std_logic_1164.all;

ENTITY ssddecoder IS
  PORT (
  enable: in std_logic;
  code: in std_logic_vector(3 downto 0);
  decode_ssd: out std_logic_vector(6 downto 0) --abcdefg
    );
END ssddecoder;

--------------------------------------------------------------------------------
--Complete your VHDL description below
--------------------------------------------------------------------------------

ARCHITECTURE behavioral OF ssddecoder IS

BEGIN

process(enable, code)
begin
	if enable = '1' then
		case code is
			when "0000" => decode_ssd<="0000001";
			when "0001" => decode_ssd<="1001111";
			when "0010" => decode_ssd<="0101101";
			when "0011" => decode_ssd<="0000110";
			when "0100" => decode_ssd<="1101100";
			when "0101" => decode_ssd<="0100100";
			when "0110" => decode_ssd<="0100000";
			when "0111" => decode_ssd<="0001111";
			when "1000" => decode_ssd<="0000000";
			when "1001" => decode_ssd<="0000100";
			when "1111" => decode_ssd<="1111110";
			when others => decode_ssd<="1111111";
		end case;
	else decode_ssd<="0000001";
	end if;		
end process;

END behavioral;

// VHDL entity binary_bcd, as the project stores it:
library ieee;
use ieee.std_logic_1164.all;
use ieee.std_logic_unsigned.all;
 
entity binary_bcd is
    port(
        clk, reset: in std_logic;
        binary_in: in std_logic_vector(7 downto 0);
        bcd0, bcd1, bcd2, bcd3, bcd4: out std_logic_vector(3 downto 0)
    );
end binary_bcd ;
 
architecture behaviour of binary_bcd is
    type states is (start, shift, done);
    signal state, state_next: states;
 
    signal binary, binary_next: std_logic_vector(7 downto 0);
    signal bcds, bcds_reg, bcds_next: std_logic_vector(19 downto 0);
    -- output register keep output constant during conversion
    signal bcds_out_reg, bcds_out_reg_next: std_logic_vector(19 downto 0);
    -- need to keep track of shifts
    signal shift_counter, shift_counter_next: natural range 0 to 8;
begin
 
    process(clk, reset)
    begin
        if reset = '1' then
            binary <= (others => '0');
            bcds <= (others => '0');
            state <= start;
            bcds_out_reg <= (others => '0');
            shift_counter <= 0;
        elsif falling_edge(clk) then
            binary <= binary_next;
            bcds <= bcds_next;
            state <= state_next;
            bcds_out_reg <= bcds_out_reg_next;
            shift_counter <= shift_counter_next;
        end if;
    end process;
 
    convert:
    process(state, binary, binary_in, bcds, bcds_reg, shift_counter)
    begin
        state_next <= state;
        bcds_next <= bcds;
        binary_next <= binary;
        shift_counter_next <= shift_counter;
 
        case state is
            when start =>
                state_next <= shift;
                binary_next <= binary_in;
                bcds_next <= (others => '0');
                shift_counter_next <= 0;
            when shift =>
                if shift_counter = 8 then
                    state_next <= done;
                else
                    binary_next <= binary(6 downto 0) & 'L';
                    bcds_next <= bcds_reg(18 downto 0) & binary(7);
                    shift_counter_next <= shift_counter + 1;
                end if;
            when done =>
                state_next <= start;
        end case;
    end process;
 
    bcds_reg(19 downto 16) <= bcds(19 downto 16) + 3 when bcds(19 downto 16) > 4 else
                              bcds(19 downto 16);
    bcds_reg(15 downto 12) <= bcds(15 downto 12) + 3 when bcds(15 downto 12) > 4 else
                              bcds(15 downto 12);
    bcds_reg(11 downto 8) <= bcds(11 downto 8) + 3 when bcds(11 downto 8) > 4 else
                             bcds(11 downto 8);
    bcds_reg(7 downto 4) <= bcds(7 downto 4) + 3 when bcds(7 downto 4) > 4 else
                            bcds(7 downto 4);
    bcds_reg(3 downto 0) <= bcds(3 downto 0) + 3 when bcds(3 downto 0) > 4 else
                            bcds(3 downto 0);
 
    bcds_out_reg_next <= bcds when state = done else
                         bcds_out_reg;
 
    bcd4 <= bcds_out_reg(19 downto 16);
    bcd3 <= bcds_out_reg(15 downto 12);
    bcd2 <= bcds_out_reg(11 downto 8);
    bcd1 <= bcds_out_reg(7 downto 4);
    bcd0 <= bcds_out_reg(3 downto 0);
 
end behaviour;

// VHDL entity UP_COUNTER, as the project stores it:
library IEEE;
use IEEE.STD_LOGIC_1164.ALL;
use IEEE.STD_LOGIC_UNSIGNED.ALL;
-- FPGA projects using Verilog code VHDL code
-- fpga4student.com: FPGA projects, Verilog projects, VHDL projects
-- VHDL project: VHDL code for counters with testbench  
-- VHDL project: VHDL code for up counter   
entity UP_COUNTER is
    Port ( clk: in std_logic; -- clock input
           reset: in std_logic; -- reset input 
           counter: out std_logic_vector(2 downto 0) -- output 4-bit counter
     );
end UP_COUNTER;

architecture Behavioral of UP_COUNTER is
signal counter_up: std_logic_vector(16 downto 0);
begin
-- up counter
process(clk)
begin
if(rising_edge(clk)) then
    if(reset='1') then
         counter_up <= x"0";
    else
        counter_up <= counter_up + x"1";
    end if;
 end if;
end process;
 counter(2) <= counter_up(16);
 counter(1) <= counter_up(15);
 counter(0) <= counter_up(14);

end Behavioral;

// VHDL entity mux_8_la_1_4bit, as the project stores it:
LIBRARY ieee;
USE ieee.std_logic_1164.all;

ENTITY mux_8_la_1_4bit IS
  PORT (
din_0,din_1,din_2,din_3,din_4,din_5,din_6,din_7: in std_logic_vector(3 downto 0);
  		sel: in std_logic_vector(2 downto 0);
  		d_out: out std_logic_vector(3 downto 0));
END mux_8_la_1_4bit;

--------------------------------------------------------------------------------
--Complete your VHDL description below
--------------------------------------------------------------------------------

ARCHITECTURE TypeArchitecture OF mux_8_la_1_4bit IS

BEGIN
	with sel select d_out <= din_0 when "000",
						din_1 when "001",
						din_2 when "010",
						din_3 when "011",
						din_4 when "100",
						din_5 when "101",
						din_6 when "110",
						"00"&din_7 when "111",	
						"0000" when others;	

END TypeArchitecture;

// VHDL entity mux_8_la_1_7bit, as the project stores it:
LIBRARY ieee;
USE ieee.std_logic_1164.all;

ENTITY mux_8_la_1_7bit IS
  PORT (
din_0,din_1,din_2,din_3,din_4,din_5,din_6,din_7: in std_logic_vector(7 downto 0);
  		sel: in std_logic_vector(2 downto 0);
  		d_out: out std_logic_vector(7 downto 0));
END mux_8_la_1_7bit;

--------------------------------------------------------------------------------
--Complete your VHDL description below
--------------------------------------------------------------------------------

ARCHITECTURE TypeArchitecture OF mux_8_la_1_7bit IS

BEGIN
	with sel select d_out <= din_0 when "000",
						din_1 when "001",
						din_2 when "010",
						din_3 when "011",
						din_4 when "100",
						din_5 when "101",
						din_6 when "110",
						din_7 when "111",	
						"0000000" when others;	

END TypeArchitecture;

// VHDL entity mux_4_la_1_4bit, as the project stores it:
LIBRARY ieee;
USE ieee.std_logic_1164.all;

ENTITY mux_4_la_1_4bit IS
  PORT (
din_0,din_1,din_2,din_3: in std_logic_vector(3 downto 0);
  		sel: in std_logic_vector(1 downto 0);
  		d_out: out std_logic_vector(7 downto 0));
END mux_4_la_1_4bit;

--------------------------------------------------------------------------------
--Complete your VHDL description below
--------------------------------------------------------------------------------

ARCHITECTURE TypeArchitecture OF mux_4_la_1_4bit IS

BEGIN
	with sel select d_out <= din_0 when "00"
,
						"0000"&din_1 when "01",
						"0000"&din_2 when "10",
						"0000"&din_3 when "11",	
						"0000" when others;	

END TypeArchitecture;

// VHDL entity mux_4_la_1_8bit, as the project stores it:
LIBRARY ieee;
USE ieee.std_logic_1164.all;

ENTITY mux_4_la_1_8bit IS
  PORT (
din_0,din_1,din_2,din_3: in std_logic_vector(7 downto 0);
  		sel: in std_logic_vector(1 downto 0);
  		d_out: out std_logic_vector(7 downto 0));
END mux_4_la_1_8bit;

--------------------------------------------------------------------------------
--Complete your VHDL description below
--------------------------------------------------------------------------------

ARCHITECTURE TypeArchitecture OF mux_4_la_1_8bit IS

BEGIN
	with sel select d_out <= din_0 when "00"
,
						din_1 when "01",
						din_2 when "10",
						din_3 when "11",	
						"0000000" when others;	

END TypeArchitecture;

// VHDL entity debouncer_30ns, as the project stores it:
LIBRARY ieee;
USE ieee.std_logic_1164.all;

ENTITY debouncer_30ns IS
  PORT (
btn,clk: in std_logic;
  btn_db: out std_logic);
END debouncer_30ns;

--------------------------------------------------------------------------------
--Complete your VHDL description below
--------------------------------------------------------------------------------

ARCHITECTURE TypeArchitecture OF debouncer_30ns IS
	
component bist_D IS
	  PORT (
	 d,clk,r,s: in std_logic;
	  		q: out std_logic
	    );
	END component;
	signal q1, q2, q3: std_logic;
BEGIN

	d1: bist_D port map(btn,clk,'0','0',q1);
	d2: bist_D port map(q1,clk,'0','0',q2);
	d3: bist_D port map(q2,clk,'0','0',q3);

	btn_db <= (q1 and q2 and q3);
END TypeArchitecture;


LIBRARY ieee;
USE ieee.std_logic_1164.all;


ENTITY bist_D IS
  PORT (
 d,clk,r,s: in std_logic;
  		q: out std_logic
    );
END bist_D;

--------------------------------------------------------------------------------
--Complete your VHDL description below
--------------------------------------------------------------------------------

ARCHITECTURE comp OF bist_D IS

BEGIN

	process(clk)
	begin
		if rising_edge(clk) then
		if r='1' then q <= '0';
		else if s='1' then q<='1';
			else q<=d;
			end if;
		end if;
		end if;
	end process;

END comp;

// VHDL entity pwm, as the project stores it:
library ieee;
use ieee.std_logic_1164.all;
use ieee.numeric_std.all;
use ieee.std_logic_unsigned.all;

entity pwm is
  port (
    clk : in std_logic;
    rst : in std_logic;
    duty_cycle0: in std_logic_vector(7 downto 0);
    duty_cycle1: in std_logic_vector(7 downto 0);
    duty_cycle2: in std_logic_vector(7 downto 0);
    duty_cycle3: in std_logic_vector(7 downto 0);
    duty_cycle4: in std_logic_vector(7 downto 0);
    duty_cycle5: in std_logic_vector(7 downto 0);
    duty_cycle6: in std_logic_vector(7 downto 0);
    duty_cycle7: in std_logic_vector(7 downto 0);
    led_out : out std_logic_vector(7 downto 0)
  );
end pwm;

architecture rtl of pwm is

  signal pwm_cnt : std_logic_vector(7 downto 0) := (others => '0');
  signal pwm_out : std_logic_vector(7 downto 0) := (others => '0');

begin

  PWM_PROC : process(clk)
  begin
    if rising_edge(clk) then
      if rst = '1' then
        pwm_cnt <= (others => '0');
        pwm_out <= (others=>'0');

      else
          pwm_cnt <= pwm_cnt + 1;
          

          -- Wrap pwm_cnt after 2**pwm_bits - 2
          if pwm_cnt = "11111110" then
            pwm_cnt <= (others => '0');
          end if;

          if pwm_cnt < duty_cycle0 then
            pwm_out(0) <= '1';
           else
           	pwm_out(0) <= '0';
          end if;

          if pwm_cnt < duty_cycle1 then
            pwm_out(1) <= '1';
           else
           	pwm_out(1) <= '0';
          end if;

		if pwm_cnt < duty_cycle2 then
            pwm_out(2) <= '1';
           else
           	pwm_out(2) <= '0';
          end if;
          if pwm_cnt < duty_cycle3 then
            pwm_out(3) <= '1';
           else
           	pwm_out(3) <= '0';
          end if;
          if pwm_cnt < duty_cycle4 then
            pwm_out(4) <= '1';
           else
           	pwm_out(4) <= '0';
          end if;
          if pwm_cnt < duty_cycle5 then
            pwm_out(5) <= '1';
           else
           	pwm_out(5) <= '0';
          end if;
          if pwm_cnt < duty_cycle6 then
            pwm_out(6) <= '1';
           else
           	pwm_out(6) <= '0';
          end if;
          if pwm_cnt < duty_cycle7 then
            pwm_out(7) <= '1';
           else
           	pwm_out(7) <= '0';
          end if;
        end if;
      end if;
  end process;
led_out <= pwm_out;
end architecture;

// VHDL entity numarator_1s, as the project stores it:
LIBRARY ieee;
USE ieee.std_logic_1164.all;

use ieee.std_logic_unsigned.all;

ENTITY numarator_1s IS
  PORT (
clk: in std_logic;
  		en: in std_logic;
  		rst: in std_logic;
  		duty_cycle: out std_logic_vector(7 downto 0)
    );
END numarator_1s;

ARCHITECTURE TypeArchitecture OF numarator_1s IS
signal cnt: integer range 0 to 390625 := 0;
signal tmp: std_logic_vector(7 downto 0):="00000000";
BEGIN

process(clk)
begin

	if rising_edge(clk) then

		if cnt = 390625 then
			cnt <= 0;
			tmp <= tmp + 1;
		else 
			cnt <= cnt + 1;
		end if;

	end if;

end process;

duty_cycle<=tmp;
END TypeArchitecture;

// VHDL entity numarator_2s, as the project stores it:
LIBRARY ieee;
USE ieee.std_logic_1164.all;

use ieee.std_logic_unsigned.all;

ENTITY numarator_2s IS
  PORT (
clk: in std_logic;
  		en: in std_logic;
  		rst: in std_logic;
  		duty_cycle: out std_logic_vector(7 downto 0)
    );
END numarator_2s;

ARCHITECTURE TypeArchitecture OF numarator_2s IS
signal cnt: integer range 0 to 781250 := 0;
signal tmp: std_logic_vector(7 downto 0):="00000000";
BEGIN

process(clk)
begin

	if rising_edge(clk) then

		if cnt = 781250 then
			cnt <= 0;
			tmp <= tmp + 1;
		else 
			cnt <= cnt + 1;
		end if;

	end if;

end process;

duty_cycle<=tmp;
END TypeArchitecture;

// VHDL entity numarator_4s, as the project stores it:
LIBRARY ieee;
USE ieee.std_logic_1164.all;

use ieee.std_logic_unsigned.all;

ENTITY numarator_4s IS
  PORT (
clk: in std_logic;
  		en: in std_logic;
  		rst: in std_logic;
  		duty_cycle: out std_logic_vector(7 downto 0)
    );
END numarator_4s;

ARCHITECTURE TypeArchitecture OF numarator_4s IS
signal cnt: integer range 0 to 1562500 := 0;
signal tmp: std_logic_vector(7 downto 0):="00000000";
BEGIN

process(clk)
begin

	if rising_edge(clk) then

		if cnt = 1562500 then
			cnt <= 0;
			tmp <= tmp + 1;
		else 
			cnt <= cnt + 1;
		end if;

	end if;

end process;

duty_cycle<=tmp;
END TypeArchitecture;

// VHDL entity numarator_3s, as the project stores it:
LIBRARY ieee;
USE ieee.std_logic_1164.all;

use ieee.std_logic_unsigned.all;

ENTITY numarator_3s IS
  PORT (
clk: in std_logic;
  		en: in std_logic;
  		rst: in std_logic;
  		duty_cycle: out std_logic_vector(7 downto 0)
    );
END numarator_3s;

ARCHITECTURE TypeArchitecture OF numarator_3s IS
signal cnt: integer range 0 to 1171875 := 0;
signal tmp: std_logic_vector(7 downto 0):="00000000";
BEGIN

process(clk)
begin

	if rising_edge(clk) then

		if cnt = 1171875 then
			cnt <= 0;
			tmp <= tmp + 1;
		else 
			cnt <= cnt + 1;
		end if;

	end if;

end process;

duty_cycle<=tmp;
END TypeArchitecture;

// VHDL entity numarator_5s, as the project stores it:
LIBRARY ieee;
USE ieee.std_logic_1164.all;

use ieee.std_logic_unsigned.all;

ENTITY numarator_5s IS
  PORT (
clk: in std_logic;
  		en: in std_logic;
  		rst: in std_logic;
  		duty_cycle: out std_logic_vector(7 downto 0)
    );
END numarator_5s;

ARCHITECTURE TypeArchitecture OF numarator_5s IS
signal cnt: integer range 0 to 1953125 := 0;
signal tmp: std_logic_vector(7 downto 0):="00000000";
BEGIN

process(clk)
begin

	if rising_edge(clk) then

		if cnt = 1953125 then
			cnt <= 0;
			tmp <= tmp + 1;
		else 
			cnt <= cnt + 1;
		end if;

	end if;

end process;

duty_cycle<=tmp;
END TypeArchitecture;

// VHDL entity numarator_6s, as the project stores it:
LIBRARY ieee;
USE ieee.std_logic_1164.all;

use ieee.std_logic_unsigned.all;

ENTITY numarator_6s IS
  PORT (
clk: in std_logic;
  		en: in std_logic;
  		rst: in std_logic;
  		duty_cycle: out std_logic_vector(7 downto 0)
    );
END numarator_6s;

ARCHITECTURE TypeArchitecture OF numarator_6s IS
signal cnt: integer range 0 to 2343750 := 0;
signal tmp: std_logic_vector(7 downto 0):="00000000";
BEGIN

process(clk)
begin

	if rising_edge(clk) then

		if cnt = 2343750 then
			cnt <= 0;
			tmp <= tmp + 1;
		else 
			cnt <= cnt + 1;
		end if;

	end if;

end process;

duty_cycle<=tmp;
END TypeArchitecture;

// VHDL entity numarator_7s, as the project stores it:
LIBRARY ieee;
USE ieee.std_logic_1164.all;

use ieee.std_logic_unsigned.all;

ENTITY numarator_7s IS
  PORT (
clk: in std_logic;
  		en: in std_logic;
  		rst: in std_logic;
  		duty_cycle: out std_logic_vector(7 downto 0)
    );
END numarator_7s;

ARCHITECTURE TypeArchitecture OF numarator_7s IS
signal cnt: integer range 0 to 2734375 := 0;
signal tmp: std_logic_vector(7 downto 0):="00000000";
BEGIN

process(clk)
begin

	if rising_edge(clk) then

		if cnt = 2734375 then
			cnt <= 0;
			tmp <= tmp + 1;
		else 
			cnt <= cnt + 1;
		end if;

	end if;

end process;

duty_cycle<=tmp;
END TypeArchitecture;

// VHDL entity numarator_8s, as the project stores it:
LIBRARY ieee;
USE ieee.std_logic_1164.all;

use ieee.std_logic_unsigned.all;

ENTITY numarator_8s IS
  PORT (
clk: in std_logic;
  		en: in std_logic;
  		rst: in std_logic;
  		duty_cycle: out std_logic_vector(7 downto 0)
    );
END numarator_8s;

ARCHITECTURE TypeArchitecture OF numarator_8s IS
signal cnt: integer range 0 to 3125000 := 0;
signal tmp: std_logic_vector(7 downto 0):="00000000";
BEGIN

process(clk)
begin

	if rising_edge(clk) then

		if cnt = 3125000 then
			cnt <= 0;
			tmp <= tmp + 1;
		else 
			cnt <= cnt + 1;
		end if;

	end if;

end process;

duty_cycle<=tmp;
END TypeArchitecture;

// VHDL entity man_ctr, as the project stores it:
----------------------------------------------------------------------------------
-- Company: 
-- Engineer: 
-- 
-- Create Date: 05/22/2023 05:59:28 PM
-- Design Name: 
-- Module Name: man_ctr - Behavioral
-- Project Name: 
-- Target Devices: 
-- Tool Versions: 
-- Description: 
-- 
-- Dependencies: 
-- 
-- Revision:
-- Revision 0.01 - File Created
-- Additional Comments:
-- 
----------------------------------------------------------------------------------


library IEEE;
use IEEE.STD_LOGIC_1164.ALL;
use ieee.std_logic_unsigned.all;
-- Uncomment the following library declaration if using
-- arithmetic functions with Signed or Unsigned values
--use IEEE.NUMERIC_STD.ALL;

-- Uncomment the following library declaration if instantiating
-- any Xilinx leaf cells in this code.
--library UNISIM;
--use UNISIM.VComponents.all;
--COUNTER PT MOD MANUAL
entity man_ctr is
  Port (inc,dec,clk,rst,en: in std_logic;
        duty_cycle: out std_logic_vector(7 downto 0));
end man_ctr;

architecture Behavioral of man_ctr is

signal cnt: std_logic_vector(7 downto 0):= (others => '0');
begin
process(clk, inc, dec, rst)
begin
    if rst = '1' then
    
    cnt <= (others => '0');

    elsif en = '1' then 
        if rising_edge(clk) then
            if dec = '1' and not(cnt = 0) then
                cnt <= cnt - 5;
            elsif inc = '1' and not(cnt = 250) then
                cnt <= cnt + 5;
            end if;
        end if;
    end if;
  duty_cycle <= cnt;
end process;

end Behavioral;

// VHDL entity RS, as the project stores it:
--------------------------------------------------------------------------------
-- Project :
-- File    :
-- Autor   :
-- Date    :
--
--------------------------------------------------------------------------------
-- Description :
--
--------------------------------------------------------------------------------

LIBRARY ieee;
USE ieee.std_logic_1164.all;

ENTITY RS IS
  PORT (
R,S: in std_logic;
  		clk: in std_logic;
  		Q: out std_logic
  		);
END RS;

--------------------------------------------------------------------------------
--Complete your VHDL description below
--------------------------------------------------------------------------------

ARCHITECTURE TypeArchitecture OF RS IS

signal q0: std_logic := '1';
BEGIN
process(clk)
begin

	if rising_edge(clk) then

		if r = '1' and s = '0' then 
			q0 <= '0';
		elsif r='0' and s = '1' then
			q0 <= '1';
		else
			q0 <= q0;
		end if;

	end if;
	Q <= q0;
end process;

END TypeArchitecture;

// VHDL entity nr_auto, as the project stores it:
LIBRARY ieee;
USE ieee.std_logic_1164.all;

use ieee.std_logic_unsigned.all; 

ENTITY nr_auto IS
  PORT (
inc, dec , rst, clk, en: in std_logic;
  		nr: out std_logic_vector(3 downto 0)
    );
END nr_auto;

--------------------------------------------------------------------------------
--Complete your VHDL description below
--------------------------------------------------------------------------------

ARCHITECTURE TypeArchitecture OF nr_auto IS

signal tmp: std_logic_vector(3 downto 0) := (others => '0');

BEGIN

process(clk)
begin
	if rst = '1' then
			tmp <= "0001";
	elsif rising_edge(clk) then
		if en = '1' then
			if inc = '1' and tmp = 15 then
				tmp <= tmp;
			elsif inc = '1' then
				tmp <= tmp + 1;
			elsif dec = '1' and tmp = 0 then
				tmp <= tmp;
			elsif dec = '1' then
				tmp <= tmp - 1;
			else 
				tmp <= tmp;
			end if;
		end if;
		

end if;

end process;

nr <= tmp;
END TypeArchitecture;

// VHDL entity div_freq_2hz, as the project stores it:
----------------------------------------------------------------------------------
-- Company: 
-- Engineer: 
-- 
-- Create Date: 05/22/2023 06:12:10 PM
-- Design Name: 
-- Module Name: div_freq_2hz - Behavioral
-- Project Name: 
-- Target Devices: 
-- Tool Versions: 
-- Description: 
-- 
-- Dependencies: 
-- 
-- Revision:
-- Revision 0.01 - File Created
-- Additional Comments:
-- 
----------------------------------------------------------------------------------


library IEEE;
use IEEE.STD_LOGIC_1164.ALL;

-- Uncomment the following library declaration if using
-- arithmetic functions with Signed or Unsigned values
--use IEEE.NUMERIC_STD.ALL;

-- Uncomment the following library declaration if instantiating
-- any Xilinx leaf cells in this code.
--library UNISIM;
--use UNISIM.VComponents.all;

entity div_freq_2hz is
  Port (clk_100mhz: in std_logic;
        clk_2hz: out std_logic );
end div_freq_2hz;

architecture Behavioral of div_freq_2hz is
signal t: std_logic := '0';
signal cnt: integer range 0 to 25000000:= 0;
begin
    process(clk_100mhz)
    begin
        if rising_edge(clk_100mhz) then
            if(cnt = 25000000) then
            t <= not(t);
            cnt <= 0;
            else 
            cnt <= cnt + 1;
            end if;
        end if;
    end process;
    clk_2hz <= t;
end Behavioral;

// VHDL entity clk_256_pe_per_hz, as the project stores it:
LIBRARY ieee;
USE ieee.std_logic_1164.all;

use ieee.std_logic_unsigned.all;

ENTITY clk_256_pe_per_hz IS
  
  PORT (n: in std_logic_vector(3 downto 0);
  		rst: in std_logic;
  		clk_100mhz: in std_logic;
  		clk_gen: out std_logic
  );
END clk_256_pe_per_hz;

--------------------------------------------------------------------------------
--Complete your VHDL description below
--------------------------------------------------------------------------------

ARCHITECTURE TypeArchitecture OF clk_256_pe_per_hz IS

signal t: std_logic := '0';
signal a: integer ;--:= conv_integer(n)*781250;
signal cnt: integer :=0;
BEGIN
--process(n, clk_100mhz)
--begin
with n select a <=  195312 when x"2",
				292968 when x"3",
				390624 when x"4",
				488280 when x"5",
				585936 when x"6",
				683592 when x"7",
				781248 when x"8",
				878904 when x"9",
				976560 when x"a",
				1074216 when x"b",
				1171872 when x"c",
				1269528 when x"d",
				1367184 when x"e",
				1464840 when x"f",
				97656 when others;
				


process(clk_100mhz, rst)
    begin
    if(rst = '1') then
    	cnt <= 0;
    	
        elsif rising_edge(clk_100mhz) then
            if(cnt = a) then
            t <= not(t);
            cnt <= 0;
            else 
            cnt <= cnt + 1;
            end if;
        end if;
    end process;
    clk_gen <= t;


END TypeArchitecture;

// VHDL entity triangular, as the project stores it:
library IEEE;
use IEEE.STD_LOGIC_1164.ALL;
use IEEE.STD_LOGIC_ARITH.ALL;
use IEEE.STD_LOGIC_UNSIGNED.ALL;

entity triangular is
port (clk : in std_logic; 
      wave_out : out std_logic_vector(7 downto 0);
      reset :in std_logic
     );
end triangular;

architecture Behavioral of triangular is

signal count2 : integer := 0;
signal direction : std_logic := '0';

begin

process(clk,reset)
begin
if(reset = '1') then
    count2 <= 0;
elsif(rising_edge(clk)) then
    if(direction = '0') then
        if(count2 = 0) then
        direction <= '1';
        else
            count2 <= count2 - 1; --up counts from 129 to 255 and then 0 to 127
        end if;
    else
        if(count2 = 255) then
            direction <= '0';
        else
            count2 <= count2 +1; --down counts from 126 to 0 and then 255 to 128
        end if;
    end if;
        
end if;
end process;

wave_out <= conv_std_logic_vector(count2,8);

end Behavioral;

// VHDL entity mux24_8_8bit, as the project stores it:
--------------------------------------------------------------------------------
-- Project :
-- File    :
-- Autor   :
-- Date    :
--
--------------------------------------------------------------------------------
-- Description :
--
--------------------------------------------------------------------------------

LIBRARY ieee;
USE ieee.std_logic_1164.all;

ENTITY mux24_8_8bit IS
  PORT (
  ------------------------------------------------------------------------------
  --Insert input ports below
    clock      : IN  std_logic;                    -- input bit example
    val        : IN  std_logic_vector(3 DOWNTO 0); -- input vector example
  ------------------------------------------------------------------------------
  --Insert output ports below
    max        : OUT std_logic;                    -- output bit example
    cpt        : OUT std_logic_vector(3 DOWNTO 0)  -- output vector example
    );
END mux24_8_8bit;

--------------------------------------------------------------------------------
--Complete your VHDL description below
--------------------------------------------------------------------------------

ARCHITECTURE TypeArchitecture OF mux24_8_8bit IS

BEGIN


END TypeArchitecture;

// VHDL entity mux_24_la_8_8bit, as the project stores it:
LIBRARY ieee;
USE ieee.std_logic_1164.all;

ENTITY mux_24_la_8_8bit IS
  PORT (
din_0,din_1,din_2,din_3,din_4,din_5,din_6,din_7: in std_logic_vector(7 downto 0);
din_8,din_9,din_10,din_11,din_12,din_13,din_14,din_15: in std_logic_vector(7 downto 0);
din_16,din_17,din_18,din_19,din_20,din_21,din_22,din_23: in std_logic_vector(7 downto 0);
  		sel: in std_logic_vector(1 downto 0);
  		d_out0: out std_logic_vector(7 downto 0);
  		d_out1: out std_logic_vector(7 downto 0);
  		d_out2: out std_logic_vector(7 downto 0);
  		d_out3: out std_logic_vector(7 downto 0);
  		d_out4: out std_logic_vector(7 downto 0);
  		d_out5: out std_logic_vector(7 downto 0);
  		d_out6: out std_logic_vector(7 downto 0);
  		d_out7: out std_logic_vector(7 downto 0));
END  mux_24_la_8_8bit;

--------------------------------------------------------------------------------
--Complete your VHDL description below
--------------------------------------------------------------------------------

ARCHITECTURE TypeArchitecture OF  mux_24_la_8_8bit IS

BEGIN
	with sel select d_out0 <= din_0 when "00",
						din_8 when "01",
						din_16 when "10",	
						"0000000" when others;

	with sel select d_out1 <= din_1 when "00",
						din_9 when "01",
						din_17 when "10",	
						"0000000" when others;

	with sel select d_out2 <= din_2 when "00",
						din_10 when "01",
						din_18 when "10",	
						"0000000" when others;

	with sel select d_out3 <= din_3 when "00",
						din_11 when "01",
						din_19 when "10",	
						"0000000" when others;

	with sel select d_out4 <= din_4 when "00",
						din_12 when "01",
						din_20 when "10",	
						"0000000" when others;

	with sel select d_out5 <= din_5 when "00",
						din_13 when "01",
						din_21 when "10",	
						"0000000" when others;

	with sel select d_out6 <= din_6 when "00",
						din_14 when "01",
						din_22 when "10",	
						"0000000" when others;

	with sel select d_out7 <= din_7 when "00",
						din_15 when "01",
						din_23 when "10",	
						"0000000" when others;

END TypeArchitecture;

// VHDL entity UC, as the project stores it:
--------------------------------------------------------------------------------
-- Project :
-- File    :
-- Autor   :
-- Date    :
--
--------------------------------------------------------------------------------
-- Description :
--
--------------------------------------------------------------------------------

LIBRARY ieee;
USE ieee.std_logic_1164.all;

ENTITY UC IS
  PORT (inc,dec,rst,ok,clk: in std_logic;
  		mode: out std_logic_vector(1 downto 0);
  		enable_man: out std_logic;
  		enable_auto: out std_logic;
  		enable_test: out std_logic
    );
END UC;

--------------------------------------------------------------------------------
--Complete your VHDL description below
--------------------------------------------------------------------------------

ARCHITECTURE TypeArchitecture OF UC IS
type state is (s1,s2,s3,s4,s5,s6,s7,s8);
signal current_state: state:=s1;
signal next_state: state ;
BEGIN
choose_state:process(clk)
begin

case current_state is
	when s1 => if inc = '1' then next_state <= s3;
			else next_state <= s2; end if;
	when s2 => if inc = '1' then next_state <= s4;
			else next_state <= s5;end if;
	when s3 => if rst = '0' then next_state <= s3;
			else next_state <= s1;end if;
	when s4 => if ok = '1' then next_state <= s7;
			else next_state <= s8;end if;
	when s5 => if inc = '1' then next_state <= s1;
			else next_state <= s6;end if;
	when s6 => if rst = '1' then next_state <= s1;
			else next_state <= s6;end if;
	when s7 => if rst = '1' then next_state <= s1;
			else next_state <= s7;end if;
	when s8 => if rst = '1' then next_state <= s1;
			else next_state <= s8;end if;

end case;

end process;

change_outputs:process(current_state)
begin
	case current_state is
		when s3 => enable_man <= '1'; 
		when s6 => enable_test <= '1';
		when s7 => enable_auto <= '1';
		when others => enable_man <='0'; enable_test <= '0'; enable_auto <='0';
	end case;
end process;

update_state:process(clk)
begin
	if rising_edge(clk) then current_state <= next_state;
	end if;	

end process;

END TypeArchitecture;

// VHDL entity or_gate, as the project stores it:
LIBRARY ieee;
USE ieee.std_logic_1164.all;

ENTITY or_gate IS
  PORT (a,b:in std_logic;
  x: out std_logic);
END or_gate;

--------------------------------------------------------------------------------
--Complete your VHDL description below
--------------------------------------------------------------------------------

ARCHITECTURE TypeArchitecture OF or_gate IS

BEGIN
x<= a or b;

END TypeArchitecture;

// VHDL entity and_gate, as the project stores it:
--------------------------------------------------------------------------------
-- Project :
-- File    :
-- Autor   :
-- Date    :
--
--------------------------------------------------------------------------------
-- Description :
--
--------------------------------------------------------------------------------

LIBRARY ieee;
USE ieee.std_logic_1164.all;

ENTITY and_gate IS
  PORT (a,b:in std_logic;
  x: out std_logic
    );
END and_gate;

--------------------------------------------------------------------------------
--Complete your VHDL description below
--------------------------------------------------------------------------------

ARCHITECTURE TypeArchitecture OF and_gate IS

BEGIN
x<= a and b;

END TypeArchitecture;
